// Logisim project y86-emulator.circ as structural Verilog: 19 circuits, main circuit main
module main (
  input  [2:0] in_1
);

  wire clock_1_out, cond_1_out_3, fetch_1_need_registers, fetch_1_need_valc, mem_control_1_out_2,
       mem_control_1_out_3, set_cc_1_out_2;
  wire [2:0] alu_1_out_6, cc_1_out_4;
  wire [3:0] alu_fun_1_out_3, dstE, dstM, icode, ifun, regA, regB, strA, strB;
  wire [7:0] currentRom;
  wire [23:0] newPC, newpc_1_newvalp, valP;
  wire [31:0] alu_a_1_out_4, alu_b_1_out_3, mem_addr_1_out_4, mem_data_1_out_4, out, valA, valB, valC, valE,
       valM;

  mem_control mem_control_1 (.out_2(mem_control_1_out_2), .out_3(mem_control_1_out_3), .in_1(icode));
  Clock clock_1 (.out(clock_1_out));
  newPC newpc_1 (
    .newValP(newpc_1_newvalp), .icode(icode), .valP(valP), .clock(clock_1_out), .cond(cond_1_out_3),
    .valC(valC), .valM(valM));
  cond cond_1 (.in_1(ifun), .out_3(cond_1_out_3), .in_2(cc_1_out_4));
  ALU alu_1 (
    .in_2(clock_1_out), .in_1(alu_fun_1_out_3), .out_5(valE), .in_3(alu_a_1_out_4), .in_4(alu_b_1_out_3),
    .out_6(alu_1_out_6));
  CC cc_1 (.in_2(clock_1_out), .in_1(alu_1_out_6), .out_4(cc_1_out_4), .in_3(set_cc_1_out_2));
  set_CC set_cc_1 (.out_2(set_cc_1_out_2), .in_1(icode));
  ALU_A alu_a_1 (.out_4(alu_a_1_out_4), .icode(icode), .valC(valC), .valA(valA));
  fetch fetch_1 (
    .valC(valC), .clk(clock_1_out), .icode(icode), .rB(regB), .ifun(ifun), .rA(regA),
    .Need_valC(fetch_1_need_valc), .Need_registers(fetch_1_need_registers), .PC_val(newPC),
    .out_10(currentRom));
  PC pc_1 (.in_2(newpc_1_newvalp), .out_3(newPC), .clk(clock_1_out));
  memory memory_1 (
    .in_2(clock_1_out), .in_4(mem_addr_1_out_4), .in_5(mem_data_1_out_4), .out_6(valM),
    .in_1(mem_control_1_out_3), .in_3(mem_control_1_out_2));
  mem_addr mem_addr_1 (.out_4(mem_addr_1_out_4), .in_3(icode), .valE(valE), .valA(valA));
  ALU_B alu_b_1 (.out_3(alu_b_1_out_3), .in_1(icode), .in_2(valB));
  mem_data mem_data_1 (.out_4(mem_data_1_out_4), .in_3(icode), .valA(valA), .valP(valP));
  ALU_fun alu_fun_1 (.out_3(alu_fun_1_out_3), .ifun(ifun), .icode(icode));
  register register_1 (
    .ValE(valE), .ValM(valM), .in_1(in_1), .out_9(out), .valB(valB), .valA(valA), .dstE(dstE), .srcA(strA),
    .srcB(strB), .in_8(clock_1_out), .dtsM(dstM));
  decoder decoder_1 (
    .icode(icode), .rA(regA), .rB(regB), .dstE(dstE), .dtsM(dstM), .srcA(strA), .srcB(strB),
    .in_1(cond_1_out_3));
  PC_increment pc_increment_1 (
    .needValC(fetch_1_need_valc), .needRegids(fetch_1_need_registers), .valP(newPC), .out_4(valP));
  Hex_Digit_Display hex_digit_display_1 (.value(currentRom[7:4]));  // open: dp
  Hex_Digit_Display hex_digit_display_2 (.value(currentRom[3:0]));  // open: dp
  Hex_Digit_Display hex_digit_display_3 (.value(newPC[23:20]));  // open: dp
  Hex_Digit_Display hex_digit_display_4 (.value(valP[23:20]));  // open: dp
  Hex_Digit_Display hex_digit_display_5 (.value(icode));  // open: dp
  Hex_Digit_Display hex_digit_display_6 (.value(valC[23:20]));  // open: dp
  Hex_Digit_Display hex_digit_display_7 (.value(valC[27:24]));  // open: dp
  Hex_Digit_Display hex_digit_display_8 (.value(newPC[15:12]));  // open: dp
  Hex_Digit_Display hex_digit_display_9 (.value(newPC[19:16]));  // open: dp
  Hex_Digit_Display hex_digit_display_10 (.value(valP[15:12]));  // open: dp
  Hex_Digit_Display hex_digit_display_11 (.value(valP[19:16]));  // open: dp
  Hex_Digit_Display hex_digit_display_12 (.value(ifun));  // open: dp
  Hex_Digit_Display hex_digit_display_13 (.value(valC[19:16]));  // open: dp
  Hex_Digit_Display hex_digit_display_14 (.value(valC[15:12]));  // open: dp
  Hex_Digit_Display hex_digit_display_15 (.value(newPC[11:8]));  // open: dp
  Hex_Digit_Display hex_digit_display_16 (.value(newPC[7:4]));  // open: dp
  Hex_Digit_Display hex_digit_display_17 (.value(valP[7:4]));  // open: dp
  Hex_Digit_Display hex_digit_display_18 (.value(valP[11:8]));  // open: dp
  Hex_Digit_Display hex_digit_display_19 (.value(regA));  // open: dp
  Hex_Digit_Display hex_digit_display_20 (.value(valC[11:8]));  // open: dp
  Hex_Digit_Display hex_digit_display_21 (.value(valC[7:4]));  // open: dp
  Hex_Digit_Display hex_digit_display_22 (.value(newPC[3:0]));  // open: dp
  Hex_Digit_Display hex_digit_display_23 (.value(valP[3:0]));  // open: dp
  Hex_Digit_Display hex_digit_display_24 (.value(regB));  // open: dp
  Hex_Digit_Display hex_digit_display_25 (.value(valC[3:0]));  // open: dp
  Hex_Digit_Display hex_digit_display_26 (.value(strA));  // open: dp
  Hex_Digit_Display hex_digit_display_27 (.value(strB));  // open: dp
  Hex_Digit_Display hex_digit_display_28 (.value(dstE));  // open: dp
  Hex_Digit_Display hex_digit_display_29 (.value(dstM));  // open: dp
  Hex_Digit_Display hex_digit_display_30 (.value(valA[27:24]));  // open: dp
  Hex_Digit_Display hex_digit_display_31 (.value(valA[31:28]));  // open: dp
  Hex_Digit_Display hex_digit_display_32 (.value(valB[31:28]));  // open: dp
  Hex_Digit_Display hex_digit_display_33 (.value(valB[27:24]));  // open: dp
  Hex_Digit_Display hex_digit_display_34 (.value(valE[31:28]));  // open: dp
  Hex_Digit_Display hex_digit_display_35 (.value(valE[27:24]));  // open: dp
  Hex_Digit_Display hex_digit_display_36 (.value(valM[31:28]));  // open: dp
  Hex_Digit_Display hex_digit_display_37 (.value(valM[27:24]));  // open: dp
  Hex_Digit_Display hex_digit_display_38 (.value(out[31:28]));  // open: dp
  Hex_Digit_Display hex_digit_display_39 (.value(out[27:24]));  // open: dp
  Hex_Digit_Display hex_digit_display_40 (.value(valA[23:20]));  // open: dp
  Hex_Digit_Display hex_digit_display_41 (.value(valA[19:16]));  // open: dp
  Hex_Digit_Display hex_digit_display_42 (.value(valB[23:20]));  // open: dp
  Hex_Digit_Display hex_digit_display_43 (.value(valB[19:16]));  // open: dp
  Hex_Digit_Display hex_digit_display_44 (.value(valE[19:16]));  // open: dp
  Hex_Digit_Display hex_digit_display_45 (.value(valE[23:20]));  // open: dp
  Hex_Digit_Display hex_digit_display_46 (.value(valM[19:16]));  // open: dp
  Hex_Digit_Display hex_digit_display_47 (.value(valM[23:20]));  // open: dp
  Hex_Digit_Display hex_digit_display_48 (.value(out[23:20]));  // open: dp
  Hex_Digit_Display hex_digit_display_49 (.value(out[19:16]));  // open: dp
  Hex_Digit_Display hex_digit_display_50 (.value(valA[15:12]));  // open: dp
  Hex_Digit_Display hex_digit_display_51 (.value(valA[11:8]));  // open: dp
  Hex_Digit_Display hex_digit_display_52 (.value(valB[15:12]));  // open: dp
  Hex_Digit_Display hex_digit_display_53 (.value(valB[11:8]));  // open: dp
  Hex_Digit_Display hex_digit_display_54 (.value(valE[15:12]));  // open: dp
  Hex_Digit_Display hex_digit_display_55 (.value(valE[11:8]));  // open: dp
  Hex_Digit_Display hex_digit_display_56 (.value(valM[11:8]));  // open: dp
  Hex_Digit_Display hex_digit_display_57 (.value(valM[15:12]));  // open: dp
  Hex_Digit_Display hex_digit_display_58 (.value(out[15:12]));  // open: dp
  Hex_Digit_Display hex_digit_display_59 (.value(out[11:8]));  // open: dp
  Hex_Digit_Display hex_digit_display_60 (.value(valA[3:0]));  // open: dp
  Hex_Digit_Display hex_digit_display_61 (.value(valA[7:4]));  // open: dp
  Hex_Digit_Display hex_digit_display_62 (.value(valB[3:0]));  // open: dp
  Hex_Digit_Display hex_digit_display_63 (.value(valB[7:4]));  // open: dp
  Hex_Digit_Display hex_digit_display_64 (.value(valE[7:4]));  // open: dp
  Hex_Digit_Display hex_digit_display_65 (.value(valE[3:0]));  // open: dp
  Hex_Digit_Display hex_digit_display_66 (.value(valM[3:0]));  // open: dp
  Hex_Digit_Display hex_digit_display_67 (.value(valM[7:4]));  // open: dp
  Hex_Digit_Display hex_digit_display_68 (.value(out[7:4]));  // open: dp
  Hex_Digit_Display hex_digit_display_69 (.value(out[3:0]));  // open: dp

  // Other names for the same wires on the sheet: reg[2:0] = in_1

  // Notes on the sheet:
  //   PC val used to
  //   access ROM
  //   Generated PC from icode
  //   Outputs generated
  //   by fetch unit
  //   Register 0-7
  //   F signifies inactive
  //   manual register return
  //   32-bit Output/Input to Register
endmodule

module fetch (
  input  clk,
  input  [23:0] PC_val,
  output [31:0] valC,
  output Need_registers,
  output Need_valC,
  output [3:0] ifun,
  output [3:0] rB,
  output [3:0] icode,
  output [3:0] rA,
  output [7:0] out_10
);

  wire and_1_out, and_2_out, and_3_out, and_4_out, and_5_out, and_6_out, and_7_out, and_8_out, and_9_out,
       decoder_1_out0, decoder_1_out1, decoder_1_out2, decoder_1_out3, decoder_1_out4, decoder_1_out5,
       not_1_out, or_1_out;
  wire [2:0] counter_1_q, subtractor_1_out;
  wire [7:0] demultiplexer_1_out0, demultiplexer_1_out1, demultiplexer_1_out2, demultiplexer_1_out3,
       demultiplexer_1_out4, demultiplexer_1_out5, register_4_q, register_5_q;
  wire [23:0] adder_1_out, bit_extender_1_out;
  wire [31:0] register_6_q;

  Register register_1 (.D(demultiplexer_1_out0), .Q({icode, ifun}), .clk(decoder_1_out0));  // open: en, clr
  Decoder #(.select(3)) decoder_1 (
    .out0(decoder_1_out0), .out1(decoder_1_out1), .out2(decoder_1_out2), .out3(decoder_1_out3),
    .out4(decoder_1_out4), .out5(decoder_1_out5), .sel(subtractor_1_out), .en(clk));  // open: out6, out7
  Counter #(.width(3), .max('h7)) counter_1 (.Q(counter_1_q), .clk(clk));  // open: load, D, count, carry, clr
  and and_1 (and_1_out, ~icode[3], ~icode[2], ~icode[1], ~icode[0]);  // AND_Gate
  nor nor_1 (Need_registers, and_3_out, or_1_out);
  Subtractor #(.width(3)) subtractor_1 (.a(counter_1_q), .b(3'b000), .out(subtractor_1_out), .bin(clk));  // open: bout
  and and_2 (and_2_out, ~icode[3], ~icode[2], ~icode[1], icode[0]);  // AND_Gate
  Register register_2 (.D(demultiplexer_1_out1), .Q({rA, rB}), .clk(decoder_1_out1), .clr(or_1_out));  // open: en
  Demultiplexer #(.select(3), .width(8), .enable("false")) demultiplexer_1 (
    .out0(demultiplexer_1_out0), .out1(demultiplexer_1_out1), .out2(demultiplexer_1_out2),
    .out3(demultiplexer_1_out3), .out4(demultiplexer_1_out4), .out5(demultiplexer_1_out5), .in(out_10),
    .sel(subtractor_1_out));  // open: out6, out7
  assign bit_extender_1_out = {{21{1'b0}}, subtractor_1_out};  // Bit_Extender bit_extender_1
  and and_3 (and_3_out, ~icode[3], icode[2], icode[1], icode[0]);  // AND_Gate
  and and_4 (and_4_out, icode[3], ~icode[2], ~icode[1], ~icode[0]);  // AND_Gate
  or or_1 (or_1_out, and_1_out, and_2_out, and_4_out, and_5_out);
  and and_5 (and_5_out, icode[3], ~icode[2], ~icode[1], icode[0]);  // AND_Gate
  Multiplexer #(.width(32), .enable("false")) multiplexer_1 (
    .in0({register_6_q[31:24], register_5_q, register_4_q, register_6_q[7:0]}),
    .in1({register_5_q, register_4_q, register_6_q[7:0], rA, rB}), .out(valC), .sel(and_3_out));
  Register register_3 (
    .D(demultiplexer_1_out2), .Q(register_6_q[7:0]), .clk(decoder_1_out2), .clr(not_1_out));  // open: en
  Adder #(.width(24)) adder_1 (.a(bit_extender_1_out), .b(PC_val), .out(adder_1_out));  // open: cin, cout
  and and_6 (and_6_out, ~icode[3], ~icode[2], icode[1], icode[0]);  // AND_Gate
  Register register_4 (.D(demultiplexer_1_out3), .Q(register_4_q), .clk(decoder_1_out3), .clr(not_1_out));  // open: en
  and and_7 (and_7_out, ~icode[3], icode[2], ~icode[1], ~icode[0]);  // AND_Gate
  or or_2 (Need_valC, and_6_out, and_3_out, and_7_out, and_8_out, and_9_out);
  Register register_5 (.D(demultiplexer_1_out4), .Q(register_5_q), .clk(decoder_1_out4), .clr(not_1_out));  // open: en
  RAM #(.addrWidth(24)) ram_1 (.addr(adder_1_out), .data(out_10), .sel(clk), .clk(clk), .ld(clk));  // open: clr
  and and_8 (and_8_out, icode[3], icode[2], ~icode[1], ~icode[0]);  // AND_Gate
  not not_1 (not_1_out, Need_valC);
  Register register_6 (
    .D(demultiplexer_1_out5), .Q(register_6_q[31:24]), .clk(decoder_1_out5), .clr(and_3_out));  // open: en
  and and_9 (and_9_out, ~icode[3], icode[2], ~icode[1], icode[0]);  // AND_Gate
endmodule

module PC_increment (
  input  needValC,
  input  needRegids,
  input  [23:0] valP,
  output [23:0] out_4
);

  wire [23:0] adder_1_out, adder_2_out, adder_3_out, bit_extender_1_out, bit_extender_2_out,
       multiplexer_1_out, multiplier_1_out;

  Adder #(.width(24)) adder_1 (.a(valP), .b(24'h1), .out(adder_1_out));  // open: cin, cout
  assign bit_extender_1_out = {{23{1'b0}}, needValC};  // Bit_Extender bit_extender_1
  assign bit_extender_2_out = {{23{1'b0}}, needRegids};  // Bit_Extender bit_extender_2
  Multiplier #(.width(24)) multiplier_1 (.a(bit_extender_1_out), .b(24'h4), .out(multiplier_1_out));  // open: cin, cout
  Adder #(.width(24)) adder_2 (.a(bit_extender_2_out), .b(adder_1_out), .out(adder_2_out));  // open: cin, cout
  Multiplexer #(.width(24), .enable("false")) multiplexer_1 (
    .in0(adder_1_out), .in1(adder_2_out), .out(multiplexer_1_out), .sel(needRegids));
  Adder #(.width(24)) adder_3 (.a(multiplier_1_out), .b(multiplexer_1_out), .out(adder_3_out));  // open: cin, cout
  Multiplexer #(.width(24), .enable("false")) multiplexer_2 (
    .in0(multiplexer_1_out), .in1(adder_3_out), .out(out_4), .sel(needValC));

  // Notes on the sheet:
  //   valP = PC +1+r+4*i
endmodule

module PC (
  input  clk,
  input  [23:0] in_2,
  output [23:0] out_3
);

  wire and_1_out, counter_1_carry, not_1_out;
  wire [23:0] register_1_q;

  not not_1 (not_1_out, clk);
  Register #(.width(24)) register_1 (.D(in_2), .Q(register_1_q), .clk(clk));  // open: en, clr
  Counter #(.width(4), .max('h8)) counter_1 (
    .carry(counter_1_carry), .clk(clk), .clr(and_1_out));  // open: load, D, count, Q
  and and_1 (and_1_out, not_1_out, counter_1_carry);
  Register #(.width(24)) register_2 (.D(register_1_q), .Q(out_3), .clk(counter_1_carry));  // open: en, clr
endmodule

module decoder (
  input  in_1,
  input  [3:0] icode,
  input  [3:0] rA,
  input  [3:0] rB,
  output [3:0] dstE,
  output [3:0] dtsM,
  output [3:0] srcA,
  output [3:0] srcB
);

  wire decoder_1_out2, decoder_1_out3, decoder_1_out4, decoder_1_out5, decoder_1_out6, decoder_1_out7,
       nand_1_out, not_1_out, not_2_out, not_3_out, not_4_out, not_5_out, or_1_out, or_2_out, or_3_out,
       or_4_out, or_5_out;
  wire [3:0] controlled_buffer_4_out;

  Decoder #(.select(4), .enable("false")) decoder_1 (
    .out2(decoder_1_out2), .out3(decoder_1_out3), .out4(decoder_1_out4), .out5(decoder_1_out5),
    .out6(decoder_1_out6), .out7(decoder_1_out7), .sel(icode));  // open: out0, out1, out8, out9, out10, out11, out12, out13, out14, out15
  assign dstE = not_1_out ? 4'b1111 : 4'bz;  // Controlled_Buffer controlled_buffer_1
  not not_1 (not_1_out, or_1_out);
  or or_1 (or_1_out, decoder_1_out2, decoder_1_out3, decoder_1_out6);
  buf or_2 (or_2_out, decoder_1_out5);  // OR_Gate
  not not_2 (not_2_out, or_2_out);
  assign dtsM = not_2_out ? 4'b1111 : 4'bz;  // Controlled_Buffer controlled_buffer_2
  or or_3 (or_3_out, decoder_1_out2, decoder_1_out4, decoder_1_out6);
  or or_4 (or_4_out, decoder_1_out6, decoder_1_out4, decoder_1_out5);
  assign dstE = nand_1_out ? controlled_buffer_4_out : 4'bz;  // Controlled_Buffer controlled_buffer_3
  assign controlled_buffer_4_out = or_1_out ? rB : 4'bz;  // Controlled_Buffer controlled_buffer_4
  assign srcA = not_3_out ? 4'b1111 : 4'bz;  // Controlled_Buffer controlled_buffer_5
  not not_3 (not_3_out, or_3_out);
  or or_5 (or_5_out, decoder_1_out2, decoder_1_out7);
  assign dstE = not_4_out ? 4'b1111 : 4'bz;  // Controlled_Buffer controlled_buffer_6
  not not_4 (not_4_out, nand_1_out);
  assign dtsM = or_2_out ? rA : 4'bz;  // Controlled_Buffer controlled_buffer_7
  nand nand_1 (nand_1_out, or_5_out, in_1);
  assign srcA = or_3_out ? rA : 4'bz;  // Controlled_Buffer controlled_buffer_8
  assign srcB = not_5_out ? 4'b1111 : 4'bz;  // Controlled_Buffer controlled_buffer_9
  not not_5 (not_5_out, or_4_out);
  assign srcB = or_4_out ? rB : 4'bz;  // Controlled_Buffer controlled_buffer_10
endmodule

module register (
  input  [2:0] in_1,
  input  [3:0] dstE,
  input  [3:0] dtsM,
  input  [31:0] ValE,
  input  [3:0] srcA,
  input  [31:0] ValM,
  input  [3:0] srcB,
  input  in_8,
  output [31:0] out_9,
  output [31:0] valA,
  output [31:0] valB
);

  wire counter_1_carry, decoder_1_out0, decoder_1_out1, decoder_1_out2, decoder_1_out3, decoder_1_out4,
       decoder_1_out5, decoder_1_out6, decoder_1_out7, decoder_2_out0, decoder_2_out1, decoder_2_out2,
       decoder_2_out3, decoder_2_out4, decoder_2_out5, decoder_2_out6, decoder_2_out7, decoder_2_out15,
       decoder_3_out0, decoder_3_out1, decoder_3_out2, decoder_3_out3, decoder_3_out4, decoder_3_out5,
       decoder_3_out6, decoder_3_out7, decoder_3_out15, not_1_out, not_2_out, xor_1_out;
  wire [2:0] and_1_out, controlled_buffer_1_out, controlled_buffer_2_out;
  wire [31:0] controlled_buffer_3_out, controlled_buffer_7_out, controlled_buffer_8_out,
       controlled_buffer_9_out, controlled_buffer_10_out, controlled_buffer_11_out, controlled_buffer_12_out,
       controlled_buffer_13_out, controlled_buffer_14_out, register_1_q, register_2_q, register_3_q,
       register_4_q, register_5_q, register_6_q, register_7_q, register_8_q;

  xor xor_1 (xor_1_out, dtsM[3], dstE[3]);
  assign controlled_buffer_1_out = dstE[3] ? 3'b111 : 3'bz;  // Controlled_Buffer controlled_buffer_1
  assign controlled_buffer_2_out = dtsM[3] ? 3'b111 : 3'bz;  // Controlled_Buffer controlled_buffer_2
  assign controlled_buffer_3_out = dtsM[3] ? ValE : 32'bz;  // Controlled_Buffer controlled_buffer_3
  assign controlled_buffer_3_out = dstE[3] ? ValM : 32'bz;  // Controlled_Buffer controlled_buffer_4
  Decoder #(.select(3)) decoder_1 (
    .out0(decoder_1_out0), .out1(decoder_1_out1), .out2(decoder_1_out2), .out3(decoder_1_out3),
    .out4(decoder_1_out4), .out5(decoder_1_out5), .out6(decoder_1_out6), .out7(decoder_1_out7),
    .sel(and_1_out), .en(xor_1_out));
  assign and_1_out = controlled_buffer_1_out & controlled_buffer_2_out;  // AND_Gate and_1, 3 bits wide
  assign controlled_buffer_1_out = not_1_out ? dstE[2:0] : 3'bz;  // Controlled_Buffer controlled_buffer_5
  not not_1 (not_1_out, dstE[3]);
  assign controlled_buffer_2_out = not_2_out ? dtsM[2:0] : 3'bz;  // Controlled_Buffer controlled_buffer_6
  not not_2 (not_2_out, dtsM[3]);
  assign controlled_buffer_7_out = decoder_1_out0 ? controlled_buffer_3_out : 32'bz;  // Controlled_Buffer controlled_buffer_7
  assign controlled_buffer_8_out = decoder_1_out1 ? controlled_buffer_3_out : 32'bz;  // Controlled_Buffer controlled_buffer_8
  assign controlled_buffer_9_out = decoder_1_out2 ? controlled_buffer_3_out : 32'bz;  // Controlled_Buffer controlled_buffer_9
  assign controlled_buffer_10_out = decoder_1_out3 ? controlled_buffer_3_out : 32'bz;  // Controlled_Buffer controlled_buffer_10
  assign controlled_buffer_11_out = decoder_1_out4 ? controlled_buffer_3_out : 32'bz;  // Controlled_Buffer controlled_buffer_11
  assign controlled_buffer_12_out = decoder_1_out5 ? controlled_buffer_3_out : 32'bz;  // Controlled_Buffer controlled_buffer_12
  assign controlled_buffer_13_out = decoder_1_out6 ? controlled_buffer_3_out : 32'bz;  // Controlled_Buffer controlled_buffer_13
  assign controlled_buffer_14_out = decoder_1_out7 ? controlled_buffer_3_out : 32'bz;  // Controlled_Buffer controlled_buffer_14
  Register #(.width(32)) register_1 (
    .D(controlled_buffer_7_out), .en(decoder_1_out0), .Q(register_1_q), .clk(counter_1_carry));  // open: clr
  Register #(.width(32)) register_2 (
    .D(controlled_buffer_8_out), .en(decoder_1_out1), .Q(register_2_q), .clk(counter_1_carry));  // open: clr
  Register #(.width(32)) register_3 (
    .D(controlled_buffer_9_out), .en(decoder_1_out2), .Q(register_3_q), .clk(counter_1_carry));  // open: clr
  Register #(.width(32)) register_4 (
    .D(controlled_buffer_10_out), .en(decoder_1_out3), .Q(register_4_q), .clk(counter_1_carry));  // open: clr
  Register #(.width(32)) register_5 (
    .D(controlled_buffer_11_out), .en(decoder_1_out4), .Q(register_5_q), .clk(counter_1_carry));  // open: clr
  Register #(.width(32)) register_6 (
    .D(controlled_buffer_12_out), .en(decoder_1_out5), .Q(register_6_q), .clk(counter_1_carry));  // open: clr
  Register #(.width(32)) register_7 (
    .D(controlled_buffer_13_out), .en(decoder_1_out6), .Q(register_7_q), .clk(counter_1_carry));  // open: clr
  Register #(.width(32)) register_8 (
    .D(controlled_buffer_14_out), .en(decoder_1_out7), .Q(register_8_q), .clk(counter_1_carry));  // open: clr
  Counter #(.width(4), .max('h8), .ongoal("load")) counter_1 (
    .D(4'b0001), .carry(counter_1_carry), .clk(in_8));  // open: load, count, Q, clr
  Multiplexer #(.select(3), .width(32), .enable("false")) multiplexer_1 (
    .in0(register_1_q), .in1(register_2_q), .in2(register_3_q), .in3(register_4_q), .in4(register_5_q),
    .in5(register_6_q), .in6(register_7_q), .in7(register_8_q), .out(out_9), .sel(in_1));
  assign valA = decoder_2_out0 ? register_1_q : 32'bz;  // Controlled_Buffer controlled_buffer_15
  assign valA = decoder_2_out1 ? register_2_q : 32'bz;  // Controlled_Buffer controlled_buffer_16
  assign valA = decoder_2_out2 ? register_3_q : 32'bz;  // Controlled_Buffer controlled_buffer_17
  assign valA = decoder_2_out3 ? register_4_q : 32'bz;  // Controlled_Buffer controlled_buffer_18
  assign valA = decoder_2_out4 ? register_5_q : 32'bz;  // Controlled_Buffer controlled_buffer_19
  assign valA = decoder_2_out5 ? register_6_q : 32'bz;  // Controlled_Buffer controlled_buffer_20
  assign valA = decoder_2_out6 ? register_7_q : 32'bz;  // Controlled_Buffer controlled_buffer_21
  assign valA = decoder_2_out7 ? register_8_q : 32'bz;  // Controlled_Buffer controlled_buffer_22
  assign valB = decoder_3_out0 ? register_1_q : 32'bz;  // Controlled_Buffer controlled_buffer_23
  assign valB = decoder_3_out1 ? register_2_q : 32'bz;  // Controlled_Buffer controlled_buffer_24
  assign valB = decoder_3_out2 ? register_3_q : 32'bz;  // Controlled_Buffer controlled_buffer_25
  assign valB = decoder_3_out3 ? register_4_q : 32'bz;  // Controlled_Buffer controlled_buffer_26
  assign valB = decoder_3_out4 ? register_5_q : 32'bz;  // Controlled_Buffer controlled_buffer_27
  assign valB = decoder_3_out5 ? register_6_q : 32'bz;  // Controlled_Buffer controlled_buffer_28
  assign valB = decoder_3_out6 ? register_7_q : 32'bz;  // Controlled_Buffer controlled_buffer_29
  assign valB = decoder_3_out7 ? register_8_q : 32'bz;  // Controlled_Buffer controlled_buffer_30
  Decoder #(.select(4), .enable("false")) decoder_2 (
    .out0(decoder_2_out0), .out1(decoder_2_out1), .out2(decoder_2_out2), .out3(decoder_2_out3),
    .out4(decoder_2_out4), .out5(decoder_2_out5), .out6(decoder_2_out6), .out7(decoder_2_out7),
    .out15(decoder_2_out15), .sel(srcA));  // open: out8, out9, out10, out11, out12, out13, out14
  Decoder #(.select(4), .enable("false")) decoder_3 (
    .out0(decoder_3_out0), .out1(decoder_3_out1), .out2(decoder_3_out2), .out3(decoder_3_out3),
    .out4(decoder_3_out4), .out5(decoder_3_out5), .out6(decoder_3_out6), .out7(decoder_3_out7),
    .out15(decoder_3_out15), .sel(srcB));  // open: out8, out9, out10, out11, out12, out13, out14
  assign valB = decoder_3_out15 ? {32{1'b0}} : 32'bz;  // Controlled_Buffer controlled_buffer_31
  assign valA = decoder_2_out15 ? {32{1'b0}} : 32'bz;  // Controlled_Buffer controlled_buffer_32
endmodule

module ALU_fun (
  input  [3:0] ifun,
  input  [3:0] icode,
  output [3:0] out_3
);

  wire decoder_1_out2, decoder_1_out3, decoder_1_out4, decoder_1_out5, decoder_1_out6, decoder_1_out7,
       decoder_1_out8, decoder_1_out10, decoder_1_out11, or_1_out, or_2_out, or_3_out;

  assign out_3 = or_1_out ? {1'b1, ifun[2:0]} : 4'bz;  // Controlled_Buffer controlled_buffer_1
  or or_1 (or_1_out, decoder_1_out2, decoder_1_out7);
  assign out_3 = or_3_out ? ifun : 4'bz;  // Controlled_Buffer controlled_buffer_2
  assign out_3 = or_2_out ? 4'b1000 : 4'bz;  // Controlled_Buffer controlled_buffer_3
  or or_2 (or_2_out, decoder_1_out3, decoder_1_out8, decoder_1_out10, decoder_1_out11);
  or or_3 (or_3_out, decoder_1_out4, decoder_1_out6, decoder_1_out5);
  Decoder #(.select(4), .enable("false")) decoder_1 (
    .out2(decoder_1_out2), .out3(decoder_1_out3), .out4(decoder_1_out4), .out5(decoder_1_out5),
    .out6(decoder_1_out6), .out7(decoder_1_out7), .out8(decoder_1_out8), .out10(decoder_1_out10),
    .out11(decoder_1_out11), .sel(icode));  // open: out0, out1, out9, out12, out13, out14, out15
endmodule

module ALU (
  input  [3:0] in_1,
  input  in_2,
  input  [31:0] in_3,
  input  [31:0] in_4,
  output [31:0] out_5,
  output [2:0] out_6
);

  wire and_1_out, and_2_out, counter_1_carry, or_1_out;
  wire [2:0] comparator_2_gt;
  wire [3:0] register_3_q;
  wire [31:0] adder_1_out, and_3_out, divider_1_out, multiplier_1_out, register_1_q, register_2_q,
       subtractor_1_out, xor_1_out;

  Counter #(.width(3), .max('h7)) counter_1 (.carry(counter_1_carry), .clk(in_2));  // open: load, D, count, Q, clr
  Register #(.width(32)) register_1 (.D(in_3), .Q(register_1_q), .clk(counter_1_carry));  // open: en, clr
  and and_1 (and_1_out, ~in_1[3], ~in_1[2], ~in_1[1], in_1[0]);  // AND_Gate
  and and_2 (and_2_out, ~in_1[0], ~in_1[1], ~in_1[2], ~in_1[3]);  // AND_Gate
  Register #(.width(32)) register_2 (.D(in_4), .Q(register_2_q), .clk(counter_1_carry));  // open: en, clr
  or or_1 (or_1_out, and_2_out, and_1_out);
  assign out_6 = or_1_out ? comparator_2_gt : 3'bz;  // Controlled_Buffer controlled_buffer_1
  Adder #(.width(32)) adder_1 (.a(register_1_q), .b(register_2_q), .out(adder_1_out));  // open: cin, cout
  Subtractor #(.width(32)) subtractor_1 (
    .a(register_1_q), .b(register_2_q), .out(subtractor_1_out));  // open: bin, bout
  assign and_3_out = register_1_q & register_2_q;  // AND_Gate and_3, 32 bits wide
  assign xor_1_out = register_1_q ^ register_2_q;  // XOR_Gate xor_1, 32 bits wide
  Multiplier #(.width(32)) multiplier_1 (
    .a(register_1_q), .b(register_2_q), .out(multiplier_1_out));  // open: cin, cout
  Divider #(.width(32)) divider_1 (.a(register_1_q), .b(register_2_q), .out(divider_1_out));  // open: upper, rem
  Register #(.width(4)) register_3 (.D(in_1), .Q(register_3_q), .clk(in_2));  // open: en, clr
  Multiplexer #(.select(4), .width(32), .enable("false")) multiplexer_1 (
    .in0(adder_1_out), .in1(subtractor_1_out), .in2(and_3_out), .in3(xor_1_out), .in4(multiplier_1_out),
    .in5(divider_1_out), .in8(register_1_q), .out(out_5), .sel(register_3_q));  // open: in6, in7, in9, in10, in11, in12, in13, in14, in15
  Comparator #(.width(32), .mode("unsigned")) comparator_1 (
    .a(out_5), .b({32{1'b0}}), .eq(comparator_2_gt[1]));  // open: gt, lt
  Comparator #(.width(32), .mode("unsigned")) comparator_2 (
    .a(32'h80000000), .b(out_5), .gt(comparator_2_gt[0]), .lt(comparator_2_gt[2]));  // open: eq
endmodule

module ALU_A (
  input  [3:0] icode,
  input  [31:0] valA,
  input  [31:0] valC,
  output [31:0] out_4
);

  wire decoder_1_out0, decoder_1_out1, decoder_1_out2, decoder_1_out3, decoder_1_out4, decoder_1_out5,
       decoder_1_out6, decoder_1_out7, or_1_out, or_2_out, or_3_out;

  Decoder #(.select(4), .enable("false")) decoder_1 (
    .out0(decoder_1_out0), .out1(decoder_1_out1), .out2(decoder_1_out2), .out3(decoder_1_out3),
    .out4(decoder_1_out4), .out5(decoder_1_out5), .out6(decoder_1_out6), .out7(decoder_1_out7), .sel(icode));  // open: out8, out9, out10, out11, out12, out13, out14, out15
  or or_1 (or_1_out, decoder_1_out0, decoder_1_out1);
  or or_2 (or_2_out, decoder_1_out7, decoder_1_out4, decoder_1_out3, decoder_1_out5);
  assign out_4 = or_1_out ? {32{1'b0}} : 32'bz;  // Controlled_Buffer controlled_buffer_1
  assign out_4 = or_2_out ? valC : 32'bz;  // Controlled_Buffer controlled_buffer_2
  or or_3 (or_3_out, decoder_1_out6, decoder_1_out2);
  assign out_4 = or_3_out ? valA : 32'bz;  // Controlled_Buffer controlled_buffer_3
endmodule

module newPC (
  input  clock,
  input  cond,
  input  [23:0] valP,
  input  [31:0] valC,
  input  [31:0] valM,
  input  [3:0] icode,
  output [23:0] newValP
);

  wire and_1_out, counter_1_carry, decoder_1_out0, decoder_1_out1, decoder_1_out2, decoder_1_out3,
       decoder_1_out4, decoder_1_out5, decoder_1_out6, decoder_1_out7, not_1_out, not_2_out, or_1_out;
  wire [23:0] bit_extender_1_out, controlled_buffer_1_out, register_1_q;

  Decoder #(.select(4)) decoder_1 (
    .out0(decoder_1_out0), .out1(decoder_1_out1), .out2(decoder_1_out2), .out3(decoder_1_out3),
    .out4(decoder_1_out4), .out5(decoder_1_out5), .out6(decoder_1_out6), .out7(decoder_1_out7), .sel(icode));  // open: out8, out9, out10, out11, out12, out13, out14, out15, en
  Counter #(.width(3), .max('h7)) counter_1 (
    .carry(counter_1_carry), .clk(clock), .clr(decoder_1_out0));  // open: load, D, count, Q
  assign controlled_buffer_1_out = or_1_out ? valP : 24'bz;  // Controlled_Buffer controlled_buffer_1
  or or_1 (or_1_out, decoder_1_out1, decoder_1_out2, decoder_1_out3, decoder_1_out4, decoder_1_out5, decoder_1_out6, not_1_out);
  not not_1 (not_1_out, cond);
  Register #(.width(24)) register_1 (
    .D(controlled_buffer_1_out), .Q(register_1_q), .clk(counter_1_carry));  // open: en, clr
  assign newValP = decoder_1_out0 ? register_1_q : 24'bz;  // Controlled_Buffer controlled_buffer_2
  assign newValP = not_2_out ? controlled_buffer_1_out : 24'bz;  // Controlled_Buffer controlled_buffer_3
  not not_2 (not_2_out, decoder_1_out0);
  and and_1 (and_1_out, decoder_1_out7, cond);
  assign controlled_buffer_1_out = and_1_out ? bit_extender_1_out : 24'bz;  // Controlled_Buffer controlled_buffer_4
  Bit_Extender #(.in_width(32), .out_width(24)) bit_extender_1 (.in(valC), .out(bit_extender_1_out));
endmodule

module ALU_B (
  input  [3:0] in_1,
  input  [31:0] in_2,
  output [31:0] out_3
);

  Multiplexer #(.select(4), .width(32), .enable("false")) multiplexer_1 (
    .in0({32{1'b0}}), .in1({32{1'b0}}), .in2({32{1'b0}}), .in3({32{1'b0}}), .in4(in_2), .in5(in_2),
    .in6(in_2), .in7({32{1'b0}}), .in8({32{1'b0}}), .in9({32{1'b0}}), .in10({32{1'b0}}), .in11({32{1'b0}}),
    .in12({32{1'b0}}), .in13({32{1'b0}}), .in14({32{1'b0}}), .in15({32{1'b0}}), .out(out_3), .sel(in_1));
endmodule

module CC (
  input  [2:0] in_1,
  input  in_2,
  input  in_3,
  output [2:0] out_4
);

  wire and_1_out;

  and and_1 (and_1_out, in_2, in_3);
  Register #(.width(1)) register_1 (.D(in_1[2]), .Q(out_4[2]), .clk(and_1_out));  // open: en, clr
  Register #(.width(1)) register_2 (.D(in_1[1]), .Q(out_4[1]), .clk(and_1_out));  // open: en, clr
  Register #(.width(1)) register_3 (.D(in_1[0]), .Q(out_4[0]), .clk(and_1_out));  // open: en, clr
endmodule

module set_CC (
  input  [3:0] in_1,
  output out_2
);

  and and_1 (out_2, ~in_1[3], in_1[2], in_1[1], ~in_1[0]);  // AND_Gate
endmodule

module cond (
  input  [3:0] in_1,
  input  [2:0] in_2,
  output out_3
);

  wire not_1_out, or_1_out, or_2_out;

  Multiplexer #(.select(4), .enable("false")) multiplexer_1 (
    .in0(1'b1), .in1(or_1_out), .in2(in_2[2]), .in3(in_2[1]), .in4(not_1_out), .in5(or_2_out), .in6(in_2[0]),
    .out(out_3), .sel(in_1));  // open: in7, in8, in9, in10, in11, in12, in13, in14, in15
  not not_1 (not_1_out, in_2[1]);
  or or_1 (or_1_out, in_2[2], in_2[1]);
  or or_2 (or_2_out, in_2[1], in_2[0]);
endmodule

module memory (
  input  in_1,
  input  in_2,
  input  in_3,
  input  [31:0] in_4,
  input  [31:0] in_5,
  output [31:0] out_6
);

  wire counter_1_carry, not_1_out, or_1_out;
  wire [23:0] bit_extender_1_out;
  wire [31:0] ram_1_data;

  Counter #(.width(4), .max('h8), .ongoal("load")) counter_1 (
    .D(4'b0001), .carry(counter_1_carry), .clk(in_2));  // open: load, count, Q, clr
  Bit_Extender #(.in_width(32), .out_width(24)) bit_extender_1 (.in(in_4), .out(bit_extender_1_out));
  or or_1 (or_1_out, in_1, in_3);
  assign out_6 = not_1_out ? {32{1'b0}} : 32'bz;  // Controlled_Buffer controlled_buffer_1
  not not_1 (not_1_out, in_1);
  RAM #(.addrWidth(24), .dataWidth(32)) ram_1 (
    .addr(bit_extender_1_out), .data(ram_1_data), .sel(or_1_out), .clk(counter_1_carry), .ld(in_1));  // open: clr
  assign out_6 = in_1 ? ram_1_data : 32'bz;  // Controlled_Buffer controlled_buffer_2
  assign ram_1_data = in_3 ? in_5 : 32'bz;  // Controlled_Buffer controlled_buffer_3
endmodule

module memory_truncate (
  input  [7:0] in_1,
  output out_2
);

  or or_1 (out_2, in_1[0], in_1[1], in_1[2], in_1[3], in_1[4], in_1[5], in_1[6], in_1[7]);
endmodule

module mem_control (
  input  [3:0] in_1,
  output out_2,
  output out_3
);

  wire decoder_1_out4, decoder_1_out5;

  Decoder #(.select(4), .enable("false")) decoder_1 (
    .out4(decoder_1_out4), .out5(decoder_1_out5), .sel(in_1));  // open: out0, out1, out2, out3, out6, out7, out8, out9, out10, out11, out12, out13, out14, out15
  buf and_1 (out_2, decoder_1_out4);  // AND_Gate
  buf and_2 (out_3, decoder_1_out5);  // AND_Gate
endmodule

module mem_addr (
  input  [31:0] valE,
  input  [31:0] valA,
  input  [3:0] in_3,
  output [31:0] out_4
);

  wire decoder_1_out4, decoder_1_out5, decoder_1_out15, or_1_out;

  Decoder #(.select(4)) decoder_1 (
    .out4(decoder_1_out4), .out5(decoder_1_out5), .out15(decoder_1_out15), .sel(in_3));  // open: out0, out1, out2, out3, out6, out7, out8, out9, out10, out11, out12, out13, out14, en
  or or_1 (or_1_out, decoder_1_out4, decoder_1_out5);
  assign out_4 = or_1_out ? valE : 32'bz;  // Controlled_Buffer controlled_buffer_1
  assign out_4 = decoder_1_out15 ? valA : 32'bz;  // Controlled_Buffer controlled_buffer_2
endmodule

module mem_data (
  input  [31:0] valA,
  input  [23:0] valP,
  input  [3:0] in_3,
  output [31:0] out_4
);

  wire decoder_1_out4;
  wire [31:0] bit_extender_1_out;

  Decoder #(.select(4), .enable("false")) decoder_1 (
    .out4(decoder_1_out4), .sel(in_3));  // open: out0, out1, out2, out3, out5, out6, out7, out8, out9, out10, out11, out12, out13, out14, out15
  assign out_4 = decoder_1_out4 ? valA : 32'bz;  // Controlled_Buffer controlled_buffer_1
  assign bit_extender_1_out = {{8{1'b0}}, valP};  // Bit_Extender bit_extender_1
endmodule
